# Fritzing sketch AquaBit (saved by Fritzing 0.9.3b)
circuit board: 8.46667cm x 5.64444cm

parts:
  U1 = ESP32S-HiLetgo [part_number=ESP32S-HiLetgo]
  DS1 = DS18B20 1-Wire Temperature Sensor [part_number=DS18B20]
  R1 = Resistor [tolerance=±5% resistance=4.7k package=THT]
  R2 = Resistor [tolerance=±5% resistance=220 package=THT]
  R3 = Resistor [tolerance=±5% resistance=220 package=THT]
  R4 = Resistor [tolerance=±5% resistance=220 package=THT]
  BREAKOUT1 = ULN2003A breakout board
  MOTOR1 = 28BYJ-48 Stepper Motor
  R5 = Photocell (LDR) [package=THT]
  R6 = Resistor [tolerance=±5% resistance=1k package=THT]
  IC1 = Voltage Regulator [package=78xxl]
  C1 = Ceramic Capacitor [capacitance=100nF voltage=16V package="100 mil [THT, multilayer]"]
  C2 = Ceramic Capacitor [capacitance=100nF voltage=16V package="100 mil [THT, multilayer]"]
  J2 = Screw terminal - 2 pins [package=THT]
  J3 = female pin header, 2 pins [form="♀ (female)"]
  Q1 = Basic FET N-Channel [package="TO220 [THT]"]
  Q2 = Basic FET N-Channel [package="TO220 [THT]"]
  Q3 = Basic FET N-Channel [package="TO220 [THT]"]
  LED1 = Super Flux RGB LED (com. anode)  # not connected
  LED2 = Super Flux RGB LED (com. cathode)  # not connected
  LED3 = Super Flux RGB LED (com. anode)  # not connected
  J4 = female pin header, 2 pins [form="♀ (female)"]
  J5 = female pin header, 2 pins [form="♀ (female)"]
  R7 = Resistor [tolerance=±5% resistance=220 package=THT]
  U2 = RELAY [package=relay-g5q]

nets:
  N1: U1.3.3, DS1.VDD, R1.Pin_0, R5.pin_0
  N2: U1.GPIO36, BREAKOUT1.In_4
  N3: U1.GPIO39, BREAKOUT1.In_3
  N4: U1.GPIO34, BREAKOUT1.In_2
  N5: U1.GPIO35, BREAKOUT1.In_1
  N6: U1.GPIO14, R5.pin_1, R6.Pin_0
  N7: U1.GPIO13, R7.Pin_0
  N8: U1.GPIO10, U2.COIL1
  N9: U1.VIN, J3.pin2
  N10: U1.GPIO7, DS1.DQ, R1.Pin_1
  N11: U1.GPIO1, R2.Pin_1
  N12: U1.GPIO22, R3.Pin_1
  N13: U1.GPIO23, R4.Pin_1
  GND: U1.GND, DS1.GND, R6.Pin_1, Q1.source, Q2.source, Q3.source
  N14: R2.Pin_0, Q3.gate
  N15: R3.Pin_0, Q2.gate
  N16: R4.Pin_0, Q1.gate
  N17: BREAKOUT1.RED_wire, MOTOR1.RED
  N18: BREAKOUT1.ORANGE_wire, MOTOR1.ORANGE
  N19: BREAKOUT1.YELLOW_wire, MOTOR1.YELLOW
  N20: BREAKOUT1.PINK_wire, MOTOR1.PINK
  N21: BREAKOUT1.BLUE_wire, MOTOR1.BLUE
  N22: IC1.GND, C1.0, C2.1, J2.pin2
  N23: IC1.IN, C1.1, J2.pin1, J4.pin1
  N24: IC1.OUT, C2.0, J3.pin1
  N25: Q1.drain, J4.pin2
  N26: Q2.drain, J5.pin1
  N27: Q3.drain, J5.pin2
  N28: R7.Pin_1, U2.COIL2

notes:
  temperature sensor
  DS18B20
  RGB LED
  Light sensor
  12 - GND
  power
  Stepper
  esp 8266
  IOT TUNISIA
  AeROBOTiX INSAT
  2018
  PUMP RELAY

custom parts:
  ESP32S-HiLetgo: HiLetgo ESP-WROOM-32 ESP32 ESP-32S Development Board 2.4GHz Dual-Mode WiFi + Bluetooth Dual Cores Microcontroller The ESP32 integrated with Antenna switches, RF Balun, power amplifiers, low-noise amplifiers, filters, and management modules, and the entire solution occupies the least area of PCB. 2.4 GHz Wi-Fi plus Bluetooth dual-mode chip, with TSMC Ultra-low power consumption 40nm technology,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
  ULN2003A breakout board: ULN2003A 7-way Darlington Transistor Driver on breakoutboard
